# Fritzing sketch Sketch (saved by Fritzing 1.0.2b)
breadboards: 2
perfboards: 1

parts:
  Bauteil1 = NodeESP
  R1 = Resistor [tolerance=±5% power=0.25W resistance=47k package=THT]
  R2 = Resistor [tolerance=±5% power=0.25W resistance=10k package=THT]
  R3 = Resistor [tolerance=±5% power=0.25W resistance=10k package=THT]
  R4 = Resistor [tolerance=±5% power=0.25W resistance=4.7k package=THT]
  R5 = Resistor [tolerance=±5% power=0.25W resistance=21k package=THT]
  R6 = Resistor [tolerance=±5% power=0.25W resistance=47k package=THT]
  R7 = Resistor [tolerance=±5% power=0.25W resistance=47k package=THT]
  R8 = Resistor [tolerance=±5% power=0.25W resistance=100k package=THT]
  S1 = Round Pushbutton
  S2 = Round Pushbutton
  S3 = Round Pushbutton
  S4 = Round Pushbutton
  S5 = Round Pushbutton
  S6 = Round Pushbutton
  Bauteil2 = Logic Level Converter
  Bauteil3 = Logic Level Converter
  Bauteil4 = Logic Level Converter
  J1 = Power Jack [package=power_jack_pth_lock]
  M1 = RioRand LM2596
  LED1 = smd LED [color="Red (633nm)" package="0603 [SMD]"]
  S8 = Round Pushbutton
  LED2 = smd LED [color="Red (633nm)" package="0603 [SMD]"]
  Q1 = NPN-Transistor [package="TO92 [THT]"]
  Q2 = NPN-Transistor [package="TO92 [THT]"]
  S7 = Round Pushbutton
  R11 = Resistor [tolerance=±5% power=0.25W resistance=2k package=THT]
  R12 = Resistor [tolerance=±5% power=0.25W resistance=2k package=THT]
  JP1 = Header 5x2 [package=2x5-shrouded_smd]
  R13 = Resistor [tolerance=±5% power=0.25W resistance=1M package=THT]
  R15 = Resistor [tolerance=±5% power=0.25W resistance=1M package=THT]
  R16 = Resistor [tolerance=±5% power=0.25W resistance=1M package=THT]
  R17 = Resistor [tolerance=±5% power=0.25W resistance=650k package=THT]
  C2 = Ceramic Capacitor [capacitance=100nF voltage=35V package="100 mil [THT, multilayer]"]
  Bauteil5 = Adafruit MAX98357A I2S 3W Class D Amplifier [part_number="Adafruit #3006"]
  C1 = Ceramic Capacitor [capacitance=100nF voltage=35V package="100 mil [THT, multilayer]"]
  R14 = Resistor [tolerance=±5% power=0.25W resistance=330k package=THT]
  LED3 = smd LED [color="Red (633nm)" package="0603 [SMD]"]
  Q3 = NPN-Transistor [package="TO92 [THT]"]
  R18 = Resistor [tolerance=±5% power=0.25W resistance=2k package=THT]
  R19 = Resistor [tolerance=±5% power=0.25W resistance=2.7k package=THT]
  R21 = Resistor [tolerance=±5% power=0.25W resistance=75k package=THT]
  R22 = Resistor [tolerance=±5% power=0.25W resistance=75k package=THT]
  A1 = Pcm5102A module
  SP1 = SPEAKER [package=pcb_mount_speaker]
  SPKR1 = Loudspeaker  # not connected

nets (from the breadboard view):
  N1: Bauteil1.5V, Bauteil1.EN, M1.Pin_3
  N2: Bauteil1.IO13, R12.Pin_0
  N3: Bauteil1.GND#34, J1.GND, J1.GNDBREAK, M1.Pin_4, S8.leg1, Q1.E, Q2.E, S7.leg1
  N4: Bauteil1.IO12, R11.Pin_0
  N5: Bauteil1.IO14, Bauteil2.TX_LV
  N6: Bauteil1.IO27, Bauteil2.RX_LV
  N7: Bauteil1.IO26, Bauteil2.RX2_LV
  N8: Bauteil1.IO25, Bauteil2.TX2_LV
  N9: Bauteil1.IO33, Bauteil3.TX_LV
  N10: Bauteil1.IO32, Bauteil3.RX_LV
  N11: Bauteil1.IO35, Bauteil1.IO21, Bauteil3.RX2_LV, R17.Pin_0, C1.1, R14.Pin_1
  N12: Bauteil1.IO34, R15.Pin_1, R16.Pin_0, C2.1
  N13: Bauteil1.IO39, S8.leg0, R21.Pin_0
  N14: Bauteil1.IO36, S7.leg0, R22.Pin_0
  N15: Bauteil1.3.3V, R1.Pin_0, R21.Pin_1, R22.Pin_1, A1.Pin_6
  N16: Bauteil1.IO15, Bauteil4.TX2_LV, A1.Pin_2
  N17: Bauteil1.IO4, R18.Pin_0
  N18: Bauteil1.IO16, Bauteil4.RX2_LV, A1.Pin_4
  N19: Bauteil1.IO17, Bauteil4.RX_LV, A1.Pin_3
  N20: Bauteil1.IO22, Bauteil3.TX2_LV
  GND: Bauteil1.GND#66, S3.leg0, S6.leg0, Bauteil2.GND, Bauteil3.GND, Bauteil4.GND, JP1.1, R16.Pin_1, R17.Pin_1, C2.0, Bauteil5.GAIN, C1.0, A1.Pin_5
  N21: R1.Pin_1, R2.Pin_0, S1.leg1, R15.Pin_0
  N22: R2.Pin_1, R3.Pin_0, S2.leg1
  N23: R3.Pin_1, R4.Pin_0
  N24: R4.Pin_1, R5.Pin_0, S3.leg1
  N25: R5.Pin_1, R6.Pin_0, S4.leg1
  N26: R7.Pin_0, S5.leg1
  N27: R8.Pin_1, S6.leg1
  N28: S1.leg0, S2.leg0
  N29: S4.leg0, S5.leg0
  N30: Bauteil2.TX_HV, JP1.4
  N31: Bauteil2.RX_HV, JP1.5
  N32: Bauteil2.HV, Bauteil3.HV, Bauteil4.HV, JP1.2
  N33: Bauteil2.RX2_HV, JP1.6
  N34: Bauteil2.TX2_HV, JP1.8
  N35: Bauteil3.TX_HV, JP1.7
  N36: Bauteil3.RX_HV, JP1.10
  N37: Bauteil4.RX_HV, Bauteil5.DIN
  N38: Bauteil4.RX2_HV, Bauteil5.LRCLK
  N39: Bauteil4.TX2_HV, Bauteil5.BCLK
  N40: J1.PWR, M1.Pin_1, LED1.anode, LED2.anode, R19.Pin_0
  N41: LED1.cathode, Q1.C
  N42: LED2.cathode, Q2.C
  N43: Q1.B, R11.Pin_1
  N44: Q2.B, R12.Pin_1
  N45: JP1.9, R13.Pin_0
  N46: R13.Pin_1, R14.Pin_0
  N47: Bauteil5.VO-, SP1.+
  N48: Bauteil5.VO+, SP1.-
  N49: LED3.cathode, Q3.C
  N50: LED3.anode, R19.Pin_1
  N51: Q3.B, R18.Pin_1

notes:
  Roter Buzzer
  Blauer Buzzer
  5V => 1.65V
  3.3V => 1.65V
  SDA | SCL (LCD)
  External speaker
  PCM5102A
  Internal speaker

custom parts:
  NodeESP: NodeESP This is the Fritzing part of the IoT Development Board NodeESP based on an ESP32
  Adafruit MAX98357A I2S 3W Class D Amplifier: Listen to this good news - we now have an all in one digital audio amp breakout board that works incredibly well with the Raspberry Pi! If you're looking for an easy and low cost way to get you digital sound files bumpin' then the MAX08357 I2S Amp Breakout is for you. It takes standard I2S digital audio input and, not only decodes it into analog, but also amplifies it directly into a speaker.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
  Pcm5102A module: Interface I2S PCM5102A DAC Decoder GY-PCM5102 I2S Player Module for Raspberry Pi pHAT Format Board Digital PCM5102 Audio Board.
